# Fritzing sketch Arduino_Uno_Nano (saved by Fritzing 1.0.4)

parts:
  Bauteil1 = Arduino Nano (Rev3.0)
  Bauteil2 = Arduino Uno (Rev3)
  TLE5012B1 = TLE5012B_BREAKOUT_BOARD [part_number=TLE5012BE1000MS2GOTOBO1]
  TLE5012B2 = TLE5012B_BREAKOUT_BOARD [part_number=TLE5012BE1000MS2GOTOBO1]

nets:
  GND: Bauteil1.GND, TLE5012B2.GND
  N1: Bauteil1.D10, TLE5012B2.P0.9
  N2: Bauteil1.D11/MOSI, Bauteil1.D12/MISO, TLE5012B2.P0.7
  N3: Bauteil1.5V, TLE5012B2.VDD_SENSE
  N4: Bauteil1.D13/SCK, TLE5012B2.P0.8
  N5: Bauteil2.D10_PWM/SS, TLE5012B1.P0.9
  N6: Bauteil2.D11_PWM/MOSI, Bauteil2.D12/MISO, TLE5012B1.P0.7
  N7: Bauteil2.D13/SCK, TLE5012B1.P0.8
  N8: Bauteil2.5V, TLE5012B1.VDD_SENSE
  GND_2: Bauteil2.GND, TLE5012B1.GND

custom parts:
  TLE5012B_BREAKOUT_BOARD: Infineon´s XENSIV™ TLx5012B magnetic angle sensor 2GO kit is a budget-priced entry level evaluation kit equipped with a TLE5012B /TLI5012B digital GMR angle sensor interfaced with an XMC1100 Infineon Microcontroller based on ARM Cortex M0 CPU. TLE5012B E1000 version: automotive predefined variant with SSC & IIF communication protocols
