# Fritzing sketch Multiple_SPI_Multiple_Sensors (saved by Fritzing 1.0.4)

parts:
  KIT_XMC47_RELAX_5V_AD_V1 = KIT_XMC47_RELAX_V1 [part_number=KITXMC47RELAXV1TOBO1]
  TLE5012B5 = TLE5012B_BREAKOUT_BOARD [part_number=TLE5012BE1000MS2GOTOBO1]
  TLE5012B6 = TLE5012B_BREAKOUT_BOARD [part_number=TLE5012BE1000MS2GOTOBO1]
  TLE5012B7 = TLE5012B_BREAKOUT_BOARD [part_number=TLE5012BE1000MS2GOTOBO1]
  TLE5012B8 = TLE5012B_BREAKOUT_BOARD [part_number=TLE5012BE1000MS2GOTOBO1]
  TLE5012B13 = TLE5012B_BREAKOUT_BOARD [part_number=TLE5012BE1000MS2GOTOBO1]
  TLE5012B17 = TLE5012B_BREAKOUT_BOARD [part_number=TLE5012BE1000MS2GOTOBO1]
  TLE5012B18 = TLE5012B_BREAKOUT_BOARD [part_number=TLE5012BE1000MS2GOTOBO1]
  TLE5012B19 = TLE5012B_BREAKOUT_BOARD [part_number=TLE5012BE1000MS2GOTOBO1]
  TLE5012B20 = TLE5012B_BREAKOUT_BOARD [part_number=TLE5012BE1000MS2GOTOBO1]
  TLE5012B21 = TLE5012B_BREAKOUT_BOARD [part_number=TLE5012BE1000MS2GOTOBO1]
  TLE5012B22 = TLE5012B_BREAKOUT_BOARD [part_number=TLE5012BE1000MS2GOTOBO1]
  TLE5012B23 = TLE5012B_BREAKOUT_BOARD [part_number=TLE5012BE1000MS2GOTOBO1]

nets:
  N1: KIT_XMC47_RELAX_5V_AD_V1.P3.4, TLE5012B7.P0.9
  N2: KIT_XMC47_RELAX_5V_AD_V1.P0.11, TLE5012B8.P0.9
  N3: KIT_XMC47_RELAX_5V_AD_V1.P0.5, TLE5012B6.P0.9
  N4: KIT_XMC47_RELAX_5V_AD_V1.P0.3, TLE5012B5.P0.9
  N5: KIT_XMC47_RELAX_5V_AD_V1.P0.1, KIT_XMC47_RELAX_5V_AD_V1.P0.0, TLE5012B5.P0.7, TLE5012B6.P0.7, TLE5012B7.P0.7, TLE5012B8.P0.7
  N6: KIT_XMC47_RELAX_5V_AD_V1.P0.10, TLE5012B5.P0.8, TLE5012B6.P0.8, TLE5012B7.P0.8, TLE5012B8.P0.8
  N7: KIT_XMC47_RELAX_5V_AD_V1.VDD5, TLE5012B5.VDD_SENSE, TLE5012B6.VDD_SENSE, TLE5012B7.VDD_SENSE, TLE5012B8.VDD_SENSE, TLE5012B13.VDD_SENSE, TLE5012B17.VDD_SENSE, TLE5012B18.VDD_SENSE, TLE5012B19.VDD_SENSE, TLE5012B20.VDD_SENSE, TLE5012B21.VDD_SENSE, TLE5012B22.VDD_SENSE, TLE5012B23.VDD_SENSE
  GND: KIT_XMC47_RELAX_5V_AD_V1.GND, TLE5012B5.GND, TLE5012B6.GND, TLE5012B7.GND, TLE5012B8.GND, TLE5012B13.GND, TLE5012B17.GND, TLE5012B18.GND, TLE5012B19.GND, TLE5012B20.GND, TLE5012B21.GND, TLE5012B22.GND, TLE5012B23.GND
  N8: KIT_XMC47_RELAX_5V_AD_V1.P3.13, TLE5012B13.P0.8, TLE5012B17.P0.8, TLE5012B18.P0.8, TLE5012B19.P0.8
  N9: KIT_XMC47_RELAX_5V_AD_V1.P3.12, KIT_XMC47_RELAX_5V_AD_V1.P3.11, TLE5012B13.P0.7, TLE5012B17.P0.7, TLE5012B18.P0.7, TLE5012B19.P0.7
  N10: KIT_XMC47_RELAX_5V_AD_V1.P0.12, TLE5012B13.P0.9
  N11: KIT_XMC47_RELAX_5V_AD_V1.P0.15, TLE5012B17.P0.9
  N12: KIT_XMC47_RELAX_5V_AD_V1.P3.3, TLE5012B18.P0.9
  N13: KIT_XMC47_RELAX_5V_AD_V1.P0.8, TLE5012B19.P0.9
  N14: KIT_XMC47_RELAX_5V_AD_V1.P1.9*, TLE5012B22.P0.9
  N15: KIT_XMC47_RELAX_5V_AD_V1.P1.10*, TLE5012B23.P0.9
  N16: KIT_XMC47_RELAX_5V_AD_V1.P1.11*, TLE5012B21.P0.9
  N17: KIT_XMC47_RELAX_5V_AD_V1.P3.10*, TLE5012B20.P0.9
  N18: KIT_XMC47_RELAX_5V_AD_V1.P3.8*, KIT_XMC47_RELAX_5V_AD_V1.P3.7*, TLE5012B20.P0.7, TLE5012B21.P0.7, TLE5012B22.P0.7, TLE5012B23.P0.7
  N19: KIT_XMC47_RELAX_5V_AD_V1.P3.9*, TLE5012B20.P0.8, TLE5012B21.P0.8, TLE5012B22.P0.8, TLE5012B23.P0.8

notes:
  SPI2 CS1<module fritzingVersion="1.0.4.2024-10-07.1.0.4rc1-4-ga8c6ef7c">
  <boundingRects>
  <boundingRect name="Leiterplattenansicht" rect="0 0 0 0"/>
  <boundingRect name="Steckplatinenansicht" rect="522 -580 64.5 36"/>
  <boundingRect name="Schaltplanansicht" rect="0 0 0 0"/>
  </boundingRects>
  <instances>
  <instance modelIndex="85519393" moduleIdRef="NoteModuleID" path=":/resources/parts/core/note.fzp">
  <title>Note2</title>
  <text>&lt;!DOCTYPE HTML PUBLIC "-//W3C//DTD HTML 4.0//EN" "http://www.w3.org/TR/REC-html40/strict.dtd">
  &lt;html>&lt;head>&lt;meta name="qrichtext" content="1" />&lt;meta charset="utf-8" />&lt;style type="text/css">
  p, li { white-space: pre-wrap; }
  hr { height: 1px; border-width: 0; }
  li.unchecked::marker { content: "\2610"; }
  li.checked::marker { content: "\2612"; }
  &lt;/style>&lt;/head>&lt;body style=" font-family:'Droid Sans'; font-size:9pt; font-weight:400; font-style:normal;">
  &lt;p style=" margin-top:0px; margin-bottom:0px; margin-left:0px; margin-right:0px; -qt-block-indent:0; text-indent:0px;">SPI2 CS1&lt;/p>&lt;/body>&lt;/html></text>
  <views>
  <breadboardView layer="breadboardNote">
  <geometry height="36" width="64.5" x="522" y="-580" z="6.50003"/>
  </breadboardView>
  </views>
  </instance>
  </instances>
  </module>
  SPI3 CS4
  SPI3 CS3
  SPI3 CS2
  SPI3 CS1
  SPI1 CS1
  SPI1 CS2
  SPI1 CS3
  SPI1 CS4
  SPI2 CS2
  SPI2 CS4
  SPI2 CS3

custom parts:
  KIT_XMC47_RELAX_V1: ModusToolbox™ software supports application development using the XMC4700 Relax evaluation kit by providing board support package (BSP) and validated code examples to help you get started. Summary of Features: -XMC4700-F144 Microcontroller based on ARM® Cortex®-M4 @ 144MHz, 2MB Flash and 352KB RAM -On-Board Debugger -Power over USB -ESD and reverse current protection -2 x user button and 2 x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
  TLE5012B_BREAKOUT_BOARD: Infineon´s XENSIV™ TLx5012B magnetic angle sensor 2GO kit is a budget-priced entry level evaluation kit equipped with a TLE5012B /TLI5012B digital GMR angle sensor interfaced with an XMC1100 Infineon Microcontroller based on ARM Cortex M0 CPU. TLE5012B E1000 version: automotive predefined variant with SSC & IIF communication protocols
