# Fritzing sketch Multiple_Sensors (saved by Fritzing 1.0.4)
circuit board: 8.46667cm x 5.64444cm

parts:
  Bauteil1 = BOOT_KIT_XMC1100 [part_number=KITXMC11BOOT001TOBO1]
  TLE5012B1 = TLE5012B_BREAKOUT_BOARD [part_number=TLE5012BE1000MS2GOTOBO1]
  TLE5012B2 = TLE5012B_BREAKOUT_BOARD [part_number=TLE5012BE1000MS2GOTOBO1]
  TLE5012B3 = TLE5012B_BREAKOUT_BOARD [part_number=TLE5012BE1000MS2GOTOBO1]
  TLE5012B4 = TLE5012B_BREAKOUT_BOARD [part_number=TLE5012BE1000MS2GOTOBO1]

nets:
  N1: Bauteil1.P0.7, TLE5012B1.P0.8, TLE5012B2.P0.8, TLE5012B3.P0.8, TLE5012B4.P0.8
  N2: Bauteil1.P1.0, Bauteil1.P1.1, TLE5012B1.P0.7, TLE5012B2.P0.7, TLE5012B3.P0.7, TLE5012B4.P0.7
  N3: Bauteil1.P0.9, TLE5012B1.P0.9
  N4: Bauteil1.P0.8, TLE5012B2.P0.9
  N5: Bauteil1.P0.12, TLE5012B3.P0.9
  N6: Bauteil1.P0.4, TLE5012B4.P0.9
  N7: Bauteil1.3V3, TLE5012B1.VDD_SENSE, TLE5012B2.VDD_SENSE, TLE5012B3.VDD_SENSE, TLE5012B4.VDD_SENSE
  GND: Bauteil1.GND, TLE5012B1.GND, TLE5012B2.GND, TLE5012B3.GND, TLE5012B4.GND

notes:
  Sensor on CS1
  Sensor on CS2
  Sensor on CS3
  Sensor on CS4

custom parts:
  BOOT_KIT_XMC1100: The XMC1100 CPU Card for Arduino TM has two rows of pin headers which fully compatible with Arduino TM shield . Hence, user can buy various Arduino shield boards off - the - shelf to test the capabilities of XMC1100 Microcontroller. ModusToolbox™ software supports application development using the XMC1100 evaluation kit by providing board support package (BSP) and validated code examples to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
  TLE5012B_BREAKOUT_BOARD: Infineon´s XENSIV™ TLx5012B magnetic angle sensor 2GO kit is a budget-priced entry level evaluation kit equipped with a TLE5012B /TLI5012B digital GMR angle sensor interfaced with an XMC1100 Infineon Microcontroller based on ARM Cortex M0 CPU. TLE5012B E1000 version: automotive predefined variant with SSC & IIF communication protocols
