# Fritzing sketch NodeMCU_ESP8266 (saved by Fritzing 1.0.4)

parts:
  Mod1 = Amica NodeMCU DEVKIT 1.0
  TLE5012B1 = TLE5012B_BREAKOUT_BOARD [part_number=TLE5012BE1000MS2GOTOBO1]
  R1 = Resistor [tolerance=±5% resistance=1k package="0805 [SMD]"]

nets:
  N1: Mod1.pin1, Mod1.pin_10, TLE5012B1.VDD_SENSE
  N2: Mod1.pin2, TLE5012B1.GND
  N3: Mod1.pin5, TLE5012B1.P0.8
  N4: Mod1.pin6, R1.Pin_0
  N5: Mod1.pin7, TLE5012B1.P0.7, R1.Pin_1
  N6: Mod1.pin8, TLE5012B1.P0.9

notes:
  1kΩ between MOSI and MISO
  100000 baud speed on serial terminal not possible

custom parts:
  TLE5012B_BREAKOUT_BOARD: Infineon´s XENSIV™ TLx5012B magnetic angle sensor 2GO kit is a budget-priced entry level evaluation kit equipped with a TLE5012B /TLI5012B digital GMR angle sensor interfaced with an XMC1100 Infineon Microcontroller based on ARM Cortex M0 CPU. TLE5012B E1000 version: automotive predefined variant with SSC & IIF communication protocols
