# Fritzing sketch WEMOS_ESP8266_EPS32 (saved by Fritzing 1.0.4)

parts:
  A1 = MH-ET Live Minikit for ESP32
  TLE5012B1 = TLE5012B_BREAKOUT_BOARD [part_number=TLE5012BE1000MS2GOTOBO1]
  R1 = Resistor [tolerance=±5% resistance=1k package="0805 [SMD]"]
  M1 = WeMos D1 Mini V3.1.0
  TLE5012B2 = TLE5012B_BREAKOUT_BOARD [part_number=TLE5012BE1000MS2GOTOBO1]
  R2 = Resistor [tolerance=±5% resistance=1k package="0805 [SMD]"]

nets:
  N1: A1.IO18, TLE5012B1.P0.8
  N2: A1.IO19, TLE5012B1.P0.7, R1.Pin_0
  N3: A1.IO23, R1.Pin_1
  N4: A1.IO5, TLE5012B1.P0.9
  N5: A1.3.3V, TLE5012B1.VDD_SENSE
  GND: A1.GND, TLE5012B1.GND
  N6: M1.D5, TLE5012B2.P0.8
  N7: M1.D6, TLE5012B2.P0.7, R2.Pin_0
  N8: M1.D7, R2.Pin_1
  N9: M1.D8, TLE5012B2.P0.9
  N10: M1.3V3, TLE5012B2.VDD_SENSE
  N11: M1.G, TLE5012B2.GND

notes:
  1kΩ between MOSI and MISO
  3.3V or 5V possible

custom parts:
  MH-ET Live Minikit for ESP32: MH-ET Live Minikit for ESP32 ( http://mh.nodebb.com/topic/8/mh-et-live-minikit-for-esp32/2/) PCB footprint is invalid.
  TLE5012B_BREAKOUT_BOARD: Infineon´s XENSIV™ TLx5012B magnetic angle sensor 2GO kit is a budget-priced entry level evaluation kit equipped with a TLE5012B /TLI5012B digital GMR angle sensor interfaced with an XMC1100 Infineon Microcontroller based on ARM Cortex M0 CPU. TLE5012B E1000 version: automotive predefined variant with SSC & IIF communication protocols
  WeMos D1 Mini V3.1.0: The D1 mini is a mini wifi board based on ESP-8266EX.
